// Logisim project control-logic.circ as structural Verilog: 1 circuit, main circuit control_logic
module control_logic (
  input  [31:0] Instruction,
  input  BrEq,
  input  BrLt,
  output PCSel,
  output RegWEn,
  output [2:0] ImmSel,
  output BrUn,
  output ASel,
  output BSel,
  output [3:0] ALUSel,
  output MemWEn,
  output [1:0] WBSel
);

  wire and_7_out, and_8_out, and_9_out, and_17_out, and_18_out, and_19_out, and_24_out, and_26_out,
       and_28_out, and_30_out, and_32_out, comparator_10_eq, comparator_11_eq, comparator_12_eq,
       comparator_13_eq, comparator_14_eq, comparator_15_eq, comparator_16_eq, comparator_17_eq,
       comparator_18_eq, comparator_19_eq, comparator_20_eq, comparator_21_eq, comparator_22_eq,
       comparator_23_eq, comparator_24_eq, comparator_25_eq, comparator_26_eq, comparator_27_eq,
       comparator_28_eq, comparator_29_eq, comparator_30_eq, comparator_31_eq, comparator_32_eq,
       comparator_33_eq, comparator_34_eq, comparator_35_eq, comparator_36_eq, comparator_37_eq,
       comparator_38_eq, comparator_39_eq, comparator_40_eq, comparator_41_eq, comparator_42_eq,
       comparator_43_eq, comparator_44_eq, comparator_45_eq, comparator_46_eq, comparator_47_eq,
       comparator_48_eq, comparator_49_eq, comparator_50_eq, comparator_51_eq, comparator_52_eq, is_b, is_i,
       is_jalr, is_l, is_r, is_s, isAdd, isAddi, isAnd, isAndi, isAuipc, isBeq, isBge, isBgeu, isBlt, isBltu,
       isBne, isJal, isJalr, isLb, isLh, isLui, isLw, isMul, isMulh, isMulhu, isOr, isOri, isSb, isSh, isSll,
       isSlli, isSlt, isSlti, isSra, isSrai, isSrl, isSrli, isSub, isSw, isXor, isXori, multiplexer_2_out,
       not_1_out, not_2_out, or_1_out, or_2_out, or_3_out, or_4_out;
  wire [1:0] priority_encoder_1_out;
  wire [4:0] bit_extender_1_out, priority_encoder_2_out;
  wire [5:0] bit_extender_2_out, bit_extender_3_out, ROMIn;
  wire [15:14] rom_1_data;

  ROM #(.addrWidth(6), .dataWidth(16)) rom_1 (
    .addr(ROMIn), .data({rom_1_data, WBSel, MemWEn, ALUSel, BSel, ASel, BrUn, ImmSel, RegWEn}));
  Priority_Encoder #(.select_enc(2)) priority_encoder_1 (
    .in0(isAuipc), .in1(isLui), .in2(isJal), .in3(isJalr), .out(priority_encoder_1_out));  // open: gs, en_out, en_in
  Priority_Encoder #(.select_enc(5)) priority_encoder_2 (
    .in0(isAdd), .in1(isMul), .in2(isSub), .in3(isSll), .in4(isMulh), .in5(isMulhu), .in6(isSlt),
    .in7(isXor), .in8(isSrl), .in9(isSra), .in10(isOr), .in11(isAnd), .in12(isLb), .in13(isLh), .in14(isLw),
    .in15(isAddi), .in16(isSlli), .in17(isSlti), .in18(isXori), .in19(isSrli), .in20(isSrai), .in21(isOri),
    .in22(isAndi), .in23(isSb), .in24(isSh), .in25(isSw), .in26(isBeq), .in27(isBne), .in28(isBlt),
    .in29(isBge), .in30(isBltu), .in31(isBgeu), .out(priority_encoder_2_out));  // open: gs, en_out, en_in
  assign bit_extender_1_out = {{3{1'b0}}, priority_encoder_1_out};  // Bit_Extender bit_extender_1
  assign bit_extender_2_out = {{1{1'b1}}, bit_extender_1_out};  // Bit_Extender bit_extender_2
  assign bit_extender_3_out = {{1{1'b0}}, priority_encoder_2_out};  // Bit_Extender bit_extender_3
  or or_1 (or_1_out, isAuipc, isLui);
  or or_2 (or_2_out, isJal, isJalr);
  or or_3 (or_3_out, or_1_out, or_2_out);
  Comparator #(.width(7)) comparator_1 (.a(7'b0010011), .b(Instruction[6:0]), .eq(is_i));  // open: gt, lt
  Comparator #(.width(7)) comparator_2 (.a(7'b0110011), .b(Instruction[6:0]), .eq(is_r));  // open: gt, lt
  Comparator #(.width(7)) comparator_3 (.a(7'b1100011), .b(Instruction[6:0]), .eq(is_b));  // open: gt, lt
  Comparator #(.width(7)) comparator_4 (.a(7'b0000011), .b(Instruction[6:0]), .eq(is_l));  // open: gt, lt
  Comparator #(.width(7)) comparator_5 (.a(7'b0100011), .b(Instruction[6:0]), .eq(is_s));  // open: gt, lt
  Comparator #(.width(7)) comparator_6 (.a(7'b1101111), .b(Instruction[6:0]), .eq(isJal));  // open: gt, lt
  Comparator #(.width(7)) comparator_7 (.a(7'b1100111), .b(Instruction[6:0]), .eq(is_jalr));  // open: gt, lt
  Comparator #(.width(7)) comparator_8 (.a(7'b0010111), .b(Instruction[6:0]), .eq(isAuipc));  // open: gt, lt
  Comparator #(.width(7)) comparator_9 (.a(7'b0110111), .b(Instruction[6:0]), .eq(isLui));  // open: gt, lt
  Multiplexer #(.width(6)) multiplexer_1 (
    .in0(bit_extender_3_out), .in1(bit_extender_2_out), .out(ROMIn), .sel(or_3_out));
  Comparator #(.width(3)) comparator_10 (.a(Instruction[14:12]), .b(3'b000), .eq(comparator_10_eq));  // open: gt, lt
  Comparator #(.width(3)) comparator_11 (.a(Instruction[14:12]), .b(3'b001), .eq(comparator_11_eq));  // open: gt, lt
  Comparator #(.width(3)) comparator_12 (.a(Instruction[14:12]), .b(3'b010), .eq(comparator_12_eq));  // open: gt, lt
  Comparator #(.width(3)) comparator_13 (.a(Instruction[14:12]), .b(3'b100), .eq(comparator_13_eq));  // open: gt, lt
  Comparator #(.width(3)) comparator_14 (.a(Instruction[14:12]), .b(3'b110), .eq(comparator_14_eq));  // open: gt, lt
  Comparator #(.width(3)) comparator_15 (.a(Instruction[14:12]), .b(3'b111), .eq(comparator_15_eq));  // open: gt, lt
  and and_1 (isAddi, is_i, comparator_10_eq);
  and and_2 (isSlli, is_i, comparator_11_eq);
  and and_3 (isSlti, is_i, comparator_12_eq);
  and and_4 (isXori, is_i, comparator_13_eq);
  and and_5 (isOri, is_i, comparator_14_eq);
  and and_6 (isAndi, is_i, comparator_15_eq);
  not not_1 (not_1_out, BrEq);
  not not_2 (not_2_out, BrLt);
  Multiplexer #(.select(3)) multiplexer_2 (
    .in0(BrEq), .in1(not_1_out), .in4(BrLt), .in5(not_2_out), .in6(BrLt), .in7(not_2_out),
    .out(multiplexer_2_out), .sel(Instruction[14:12]));  // open: in2, in3
  Comparator #(.width(3)) comparator_16 (.a(Instruction[14:12]), .b(3'b101), .eq(comparator_16_eq));  // open: gt, lt
  Comparator #(.width(7)) comparator_17 (.a(Instruction[31:25]), .b({7{1'b0}}), .eq(comparator_17_eq));  // open: gt, lt
  Comparator #(.width(3)) comparator_18 (.a(Instruction[14:12]), .b(3'b101), .eq(comparator_18_eq));  // open: gt, lt
  Comparator #(.width(7)) comparator_19 (
    .a(Instruction[31:25]), .b(7'b0100000), .eq(comparator_19_eq));  // open: gt, lt
  and and_7 (and_7_out, is_b, multiplexer_2_out);
  or or_4 (or_4_out, isJal, isJalr);
  and and_8 (and_8_out, comparator_16_eq, comparator_17_eq);
  and and_9 (and_9_out, comparator_18_eq, comparator_19_eq);
  Comparator #(.width(3)) comparator_20 (.a(Instruction[14:12]), .b(3'b000), .eq(comparator_20_eq));  // open: gt, lt
  or or_5 (PCSel, and_7_out, or_4_out);
  and and_10 (isSrli, is_i, and_8_out);
  and and_11 (isSrai, is_i, and_9_out);
  and and_12 (isJalr, is_jalr, comparator_20_eq);
  Comparator #(.width(3)) comparator_21 (.a(Instruction[14:12]), .b(3'b010), .eq(comparator_21_eq));  // open: gt, lt
  Comparator #(.width(3)) comparator_22 (.a(Instruction[14:12]), .b(3'b011), .eq(comparator_22_eq));  // open: gt, lt
  Comparator #(.width(3)) comparator_23 (.a(Instruction[14:12]), .b(3'b100), .eq(comparator_23_eq));  // open: gt, lt
  Comparator #(.width(3)) comparator_24 (.a(Instruction[14:12]), .b(3'b111), .eq(comparator_24_eq));  // open: gt, lt
  Comparator #(.width(3)) comparator_25 (.a(Instruction[14:12]), .b(3'b101), .eq(comparator_25_eq));  // open: gt, lt
  Comparator #(.width(7)) comparator_26 (.a(Instruction[31:25]), .b({7{1'b0}}), .eq(comparator_26_eq));  // open: gt, lt
  Comparator #(.width(3)) comparator_27 (.a(Instruction[14:12]), .b(3'b101), .eq(comparator_27_eq));  // open: gt, lt
  Comparator #(.width(7)) comparator_28 (
    .a(Instruction[31:25]), .b(7'b0100000), .eq(comparator_28_eq));  // open: gt, lt
  Comparator #(.width(3)) comparator_29 (.a(Instruction[14:12]), .b(3'b110), .eq(comparator_29_eq));  // open: gt, lt
  Comparator #(.width(7)) comparator_30 (.a(Instruction[31:25]), .b({7{1'b0}}), .eq(comparator_30_eq));  // open: gt, lt
  and and_13 (isSlt, is_r, comparator_21_eq);
  and and_14 (isMulhu, is_r, comparator_22_eq);
  and and_15 (isXor, is_r, comparator_23_eq);
  and and_16 (isAnd, is_r, comparator_24_eq);
  and and_17 (and_17_out, comparator_25_eq, comparator_26_eq);
  and and_18 (and_18_out, comparator_27_eq, comparator_28_eq);
  and and_19 (and_19_out, comparator_29_eq, comparator_30_eq);
  and and_20 (isSrl, is_r, and_17_out);
  and and_21 (isSra, is_r, and_18_out);
  and and_22 (isOr, is_r, and_19_out);
  Comparator #(.width(3)) comparator_31 (.a(Instruction[14:12]), .b(3'b000), .eq(comparator_31_eq));  // open: gt, lt
  Comparator #(.width(7)) comparator_32 (.a(Instruction[31:25]), .b({7{1'b0}}), .eq(comparator_32_eq));  // open: gt, lt
  Comparator #(.width(3)) comparator_33 (.a(Instruction[14:12]), .b(3'b000), .eq(comparator_33_eq));  // open: gt, lt
  Comparator #(.width(7)) comparator_34 (
    .a(Instruction[31:25]), .b(7'b0000001), .eq(comparator_34_eq));  // open: gt, lt
  Comparator #(.width(3)) comparator_35 (.a(Instruction[14:12]), .b(3'b000), .eq(comparator_35_eq));  // open: gt, lt
  Comparator #(.width(7)) comparator_36 (
    .a(Instruction[31:25]), .b(7'b0100000), .eq(comparator_36_eq));  // open: gt, lt
  Comparator #(.width(3)) comparator_37 (.a(Instruction[14:12]), .b(3'b001), .eq(comparator_37_eq));  // open: gt, lt
  Comparator #(.width(7)) comparator_38 (.a(Instruction[31:25]), .b({7{1'b0}}), .eq(comparator_38_eq));  // open: gt, lt
  Comparator #(.width(3)) comparator_39 (.a(Instruction[14:12]), .b(3'b001), .eq(comparator_39_eq));  // open: gt, lt
  Comparator #(.width(7)) comparator_40 (
    .a(Instruction[31:25]), .b(7'b0000001), .eq(comparator_40_eq));  // open: gt, lt
  and and_23 (isAdd, is_r, and_24_out);
  and and_24 (and_24_out, comparator_31_eq, comparator_32_eq);
  and and_25 (isMul, is_r, and_26_out);
  and and_26 (and_26_out, comparator_33_eq, comparator_34_eq);
  and and_27 (isSub, is_r, and_28_out);
  and and_28 (and_28_out, comparator_35_eq, comparator_36_eq);
  and and_29 (isSll, is_r, and_30_out);
  and and_30 (and_30_out, comparator_37_eq, comparator_38_eq);
  and and_31 (isMulh, is_r, and_32_out);
  and and_32 (and_32_out, comparator_39_eq, comparator_40_eq);
  Comparator #(.width(3)) comparator_41 (.a(Instruction[14:12]), .b(3'b000), .eq(comparator_41_eq));  // open: gt, lt
  Comparator #(.width(3)) comparator_42 (.a(Instruction[14:12]), .b(3'b001), .eq(comparator_42_eq));  // open: gt, lt
  Comparator #(.width(3)) comparator_43 (.a(Instruction[14:12]), .b(3'b100), .eq(comparator_43_eq));  // open: gt, lt
  Comparator #(.width(3)) comparator_44 (.a(Instruction[14:12]), .b(3'b101), .eq(comparator_44_eq));  // open: gt, lt
  Comparator #(.width(3)) comparator_45 (.a(Instruction[14:12]), .b(3'b110), .eq(comparator_45_eq));  // open: gt, lt
  Comparator #(.width(3)) comparator_46 (.a(Instruction[14:12]), .b(3'b111), .eq(comparator_46_eq));  // open: gt, lt
  and and_33 (isBeq, is_b, comparator_41_eq);
  and and_34 (isBne, is_b, comparator_42_eq);
  and and_35 (isBlt, is_b, comparator_43_eq);
  and and_36 (isBge, is_b, comparator_44_eq);
  and and_37 (isBltu, is_b, comparator_45_eq);
  and and_38 (isBgeu, is_b, comparator_46_eq);
  Comparator #(.width(3)) comparator_47 (.a(Instruction[14:12]), .b(3'b000), .eq(comparator_47_eq));  // open: gt, lt
  Comparator #(.width(3)) comparator_48 (.a(Instruction[14:12]), .b(3'b001), .eq(comparator_48_eq));  // open: gt, lt
  Comparator #(.width(3)) comparator_49 (.a(Instruction[14:12]), .b(3'b010), .eq(comparator_49_eq));  // open: gt, lt
  Comparator #(.width(3)) comparator_50 (.a(Instruction[14:12]), .b(3'b000), .eq(comparator_50_eq));  // open: gt, lt
  Comparator #(.width(3)) comparator_51 (.a(Instruction[14:12]), .b(3'b001), .eq(comparator_51_eq));  // open: gt, lt
  Comparator #(.width(3)) comparator_52 (.a(Instruction[14:12]), .b(3'b010), .eq(comparator_52_eq));  // open: gt, lt
  and and_39 (isLb, is_l, comparator_47_eq);
  and and_40 (isLh, is_l, comparator_48_eq);
  and and_41 (isLw, is_l, comparator_49_eq);
  and and_42 (isSb, is_s, comparator_50_eq);
  and and_43 (isSh, is_s, comparator_51_eq);
  and and_44 (isSw, is_s, comparator_52_eq);

  // Other names for the same wires on the sheet: Opcode[6:0] = Instruction[6:0]; Funct3[2:0] = Instruction[14:12];
  //   Funct7[6:0] = Instruction[31:25]

  // Notes on the sheet:
  //   INPUTS to your circuit
  //   Connect ROM Input here ->
  //   contents of rom_1 (hex, n*v repeats v):
  //   1001 1401 1601 1081 1481 1581 1101 1201 1281 1681 1301 1381 41 41 41 1041 10c1 1141 1241 12c1 16c1
  //   1341 13c1 842 842 842 4*64 74 74 1067 17c7 2069 2041
  //   ROM FOR CONTROL LOGIC
  //   DON'T CHANGE THE LOCATIONS OF THE INPUTS AND OUTPUTS!
  //   This is only if you choose to do the ROM option
  //   CONNECT
  //   WIRE
  //   TO
  //   USE
  //   ROM
  //   OUTPUT from your circuit
  //   Reminder: If using ROM, use combinational logic for PCSel
endmodule
