// Logisim project partial-store.circ as structural Verilog: 1 circuit, main circuit partial_store
module partial_store (
  input  [31:0] Instruction,
  input  [31:0] MemAddress,
  input  [31:0] DataFromReg,
  input  MemWEn,
  output [3:0] MemWriteMask,
  output [31:0] DataToMem
);

  wire [3:0] ByMa, HaMa, multiplexer_3_out;
  wire [4:0] bit_extender_1_out, S;
  wire [31:0] B, bit_extender_2_out, bit_extender_3_out, H;

  Multiplexer #(.select(3), .width(32)) multiplexer_1 (
    .in0(B), .in1(H), .in2(DataFromReg), .out(DataToMem), .sel(Instruction[14:12]));  // open: in3, in4, in5, in6, in7
  Multiplexer #(.width(4)) multiplexer_2 (.in0(4'b0000), .in1(multiplexer_3_out), .out(MemWriteMask), .sel(MemWEn));
  Multiplexer #(.select(3), .width(4)) multiplexer_3 (
    .in0(ByMa), .in1(HaMa), .in2(4'b1111), .out(multiplexer_3_out), .sel(Instruction[14:12]));  // open: in3, in4, in5, in6, in7
  assign bit_extender_1_out = {{3{1'b0}}, MemAddress[1:0]};  // Bit_Extender bit_extender_1
  assign bit_extender_2_out = {{24{1'b0}}, DataFromReg[7:0]};  // Bit_Extender bit_extender_2
  assign bit_extender_3_out = {{16{1'b0}}, DataFromReg[15:0]};  // Bit_Extender bit_extender_3
  Multiplexer #(.select(2), .width(4)) multiplexer_4 (
    .in0(4'b0001), .in1(4'b0010), .in2(4'b0100), .in3(4'b1000), .out(ByMa), .sel(MemAddress[1:0]));
  Multiplexer #(.select(2), .width(4)) multiplexer_5 (
    .in0(4'b0011), .in2(4'b1100), .out(HaMa), .sel(MemAddress[1:0]));  // open: in1, in3
  Multiplier #(.width(5)) multiplier_1 (.a(bit_extender_1_out), .b(5'b01000), .out(S));  // open: cin, cout
  Shifter #(.width(32)) shifter_1 (.in(bit_extender_2_out), .\dist (S), .out(B));
  Shifter #(.width(32)) shifter_2 (.in(bit_extender_3_out), .\dist (S), .out(H));

  // Notes on the sheet:
  //   INPUTS to your circuit
  //   DON'T CHANGE THE LOCATIONS OF THE INPUTS AND OUTPUTS!
  //   OUTPUT from your circuit
endmodule
